# Fritzing sketch Example-3_Analog-Values-From-a-Potentiometer (saved by Fritzing 0.9.9b)
breadboards: 1

parts:
  Part1 = Arduino Uno (Rev3)
  LED1 = LED - 5mm [color="Red (633nm)" current=0.030 package="5 mm [THT]"]
  U1 = POT [package=pot_mammoth]
  R1 = Resistor [tolerance=±1% power=0.25 resistance=220 package=THT]

nets:
  N1: Part1.A0, U1.A
  N2: Part1.D6_PWM, R1.Pin_0
  N3: Part1.5V, U1.S
  N4: Part1.GND, LED1.cathode, U1.E
  N5: LED1.anode, R1.Pin_1
