# Fritzing sketch Example-4_Replace-Potentiometer-With-LDR (saved by Fritzing 0.9.9b)
breadboards: 1

parts:
  Part1 = Arduino Uno (Rev3)
  R1 = Photocell (LDR) [package=THT]
  LED1 = LED - 5mm [color="Red (633nm)" current=0.030 package="5 mm [THT]"]
  R3 = Resistor [tolerance=±1% power=0.25 resistance=220 package=THT]
  R2 = Resistor [tolerance=±1% power=0.25 resistance=1k package=THT]

nets:
  N1: Part1.A0, R1.pin_0, R2.Pin_1
  N2: Part1.D6_PWM, R3.Pin_0
  N3: Part1.5V, R2.Pin_0
  N4: Part1.GND, R1.pin_1, LED1.cathode
  N5: LED1.anode, R3.Pin_1

// code stored in the sketch: Eksempel4_LDR.ino
#define LEDPIN 6 // Konstanten LEDPIN er sat til 6 for PWM.

int ldrVal = 0; // En variabel integer sættes op til at holde LDR'ens værdi.
int pwmOut = 0; // En variabel integer sættes op til at holde PWM output argumentet.

void setup() {
  pinMode(LEDPIN, OUTPUT); //ledPin sættes som output.
  Serial.begin(9600); //Den serielle kommunikation mellem Arduino og Computer påbegyndes med en baudrate på 9600 baud (tegn/s)
}

void loop() {
  ldrVal = analogRead(A0); // Der foretages en analoglæsning på A0.
  Serial.print("ldrVal = "); // Værdien for aflæsningen skrives til det serielle vindue.
  Serial.println(ldrVal); // Værdien for aflæsningen skrives til det serielle vindue.

  pwmOut = map(ldrVal,1023,344,0,255); // pwmOut får værdien fra ldrVal, Det mappes inverst, ud fra LDR'ens konfiguration. Så en høj spænding giver lidt lys.
  analogWrite(LEDPIN, pwmOut); // LEDPIN genererer et PWM signel, der svarer til den dutycycle tallet fra 0-255 repræsenterer.
  Serial.println(pwmOut); 
  Serial.print("Dutycycle = "); // Dutycycle skal også leveres til Serial vinduet.
  Serial.print((float)pwmOut/255.0*100.0); // Det beregnes som en normal procentomregning udfra 255 som maksværdien.
  Serial.println("%"); // Et procenttegn på til sidst, for at gøre det pænt.
}
