# Fritzing sketch Example-3_Dot-Matrix-LCD-Printing (saved by Fritzing 0.9.9b)
breadboards: 1

parts:
  U1 = LCD-16X2 [package=lcd-16x2]
  Part1 = Arduino Uno (Rev3)
  S1 = Pushbutton [package="[THT]"]
  U2 = POT [package=pot_mammoth]
  R1 = Resistor [tolerance=±1% power=0.25 resistance=10k package=THT]
  R2 = Resistor [tolerance=±1% power=0.25 resistance=220 package=THT]

nets:
  VSS: U1.VSS, U1.R_W, U1.K, Part1.GND, U2.S, R1.Pin_0
  VDD: U1.VDD, Part1.5V, S1.Pin_3, S1.Pin_4, U2.E, R2.Pin_0
  N1: U1.VO, U2.A
  N2: U1.RS, Part1.D3_PWM
  N3: U1.E, Part1.D4
  N4: U1.DB4, Part1.D5_PWM
  N5: U1.DB5, Part1.D6_PWM
  N6: U1.DB6, Part1.D7
  N7: U1.DB7, Part1.D8
  N8: U1.A, R2.Pin_1
  N9: Part1.D2, S1.Pin_1, S1.Pin_2, R1.Pin_1

// code stored in the sketch: Eksempel4_LCD_Printing.ino
#include <LiquidCrystal.h> // Vi indlæser LiquidCrystal biblioteket.

#define RS 3
#define E 4
#define D4 5
#define D5 6
#define D6 7
#define D7 8
// RW til GND
// VSS til GND
// VDD til 5V
// 10k potmeter mellem GND VO og VDD
// A forbindes med en 220 ohms resistor til +5V og en K til GND.

#define BTN 2 // Knappen sidder på pin 2.

//Vores Helt eget tegn:
byte blinkey[8] =
{
  B00000,
  B11001,
  B00000,
  B00000,
  B11111,
  B01001,
  B00110
};

LiquidCrystal lcd(RS, E, D4, D5, D6, D7); // Vi constructer et objekt lcd af typen Liquid Crystal.

unsigned int count = 0; // count er den tællerværdi vi vil skrive ud i sidste ende.
long unsigned int wait = 0; // wait er en timervariabel, der hjælper os med at holde styr på ventetiden for knappen.

void setup() {
  pinMode(BTN, INPUT); // BTN sættes op som input.
  
  lcd.createChar(0, blinkey); // createChar funktionen bruges til at sætte vores eget tegn op.
  
  lcd.begin(16, 2); // LCD'et opsættes med 2 linjer, 16 chars.
  
  lcd.setCursor(0 /*x*/ , 0 /*y*/); // Cursoren for displayet sættes på koordinaterne 0,0.
  lcd.print("Hello world! "); // Vi udskriver Hello World.
  
  lcd.write(byte(0)); // Vi skriver vores eget tegn.
}

void loop() {
  // Vi behøver kun ændre noget, hvis der trykkes på knappen:
  if (digitalRead(BTN) == HIGH && wait <= (millis() - 100)) //Hvis knappen er høj, og ventetimeren er 100 ms efter systemtimeren.
  {
    wait = millis(); // Ventetimeren opdateres.
    count++; // Count inkrementeres med 1.
    
    lcd.setCursor(0, 1); // Sæt cursoren ned på den rigtige plads.
    lcd.print(count); // Udskriv count.
    
    while(digitalRead(BTN) == HIGH); // TRICK! Programmet laver intet i en while-løkke der bare er while(cond);
    delay(50); // Når knappen går ned fra HIGH igen, vent 50ms.
  }
}
