# Fritzing sketch Example-1_Pulse-Oximeter (saved by Fritzing 0.9.9b)
breadboards: 1

parts:
  Part1 = Arduino Uno (Rev3) - ICSP
  R2 = Resistor [tolerance=±1% power=0.25 resistance=1k package=THT]
  R3 = Resistor [tolerance=±1% power=0.25 resistance=1k package=THT]
  R4 = Resistor [tolerance=±1% power=0.25 resistance=1k package=THT]
  R5 = Resistor [tolerance=±1% power=0.25 resistance=1k package=THT]
  R6 = Resistor [tolerance=±1% power=0.25 resistance=10k package=THT]
  R7 = Resistor [tolerance=±1% power=0.25 resistance=10k package=THT]
  R8 = Resistor [tolerance=±1% power=0.25 resistance=10k package=THT]
  R9 = Resistor [tolerance=±1% power=0.25 resistance=10k package=THT]
  R10 = Resistor [tolerance=±1% power=0.25 resistance=10k package=THT]
  R11 = Resistor [tolerance=±1% power=0.25 resistance=10k package=THT]
  R12 = Resistor [tolerance=±1% power=0.25 resistance=10k package=THT]
  R13 = Resistor [tolerance=±1% power=0.25 resistance=10k package=THT]
  U1 = POT [package=pot_alpha_rv16af-20]
  Part2 = ILI9341
  M1 = MAX30102

nets:
  N1: Part1.A0, U1.S
  N2: Part1.A4/SDA, M1.SDA
  N3: Part1.A5/SCL, M1.SCL
  N4: Part1.D8, R10.Pin_0
  N5: Part1.D9_PWM, R8.Pin_0
  N6: Part1.D10_PWM/SS, R6.Pin_0
  N7: Part1.D11_PWM/MOSI, R4.Pin_0
  N8: Part1.D12/MISO, Part2.TFT_MISO, Part2.TS_MISO
  N9: Part1.D13/SCK, R3.Pin_0
  N10: Part1.D6_PWM, Part2.LED
  N11: Part1.D7, R12.Pin_0
  3V3: Part1.3V3, U1.A, Part2.VCC
  5V: Part1.5V, M1.VIN
  GND: Part1.GND, R2.Pin_0, R5.Pin_0, R7.Pin_0, R9.Pin_0, R11.Pin_0, R13.Pin_0, U1.E, Part2.GND, M1.GND
  N12: R2.Pin_1, R3.Pin_1, Part2.TFT_SCK, Part2.TS_SCK
  N13: R4.Pin_1, R5.Pin_1, Part2.TFT_MOSI, Part2.TS_MOSI
  N14: R6.Pin_1, R7.Pin_1, Part2.TFT_CS
  N15: R8.Pin_1, R9.Pin_1, Part2.TFT_RST
  N16: R10.Pin_1, R11.Pin_1, Part2.TFT_DC
  N17: R12.Pin_1, R13.Pin_1, Part2.TS_CS

custom parts:
  ILI9341: A cheap 3.3V TFT LCD 320x240 (5V VCC and backlight compatible). Uses XPT2046 touchscreen driver.
  MAX30102: Pulse-Oximeter module using the MAX30102 chip. As usual, if you want the mounting holes in pcb, you need to drag a hole over the pad in silkscreen to actually drill the hole (by default they are not drilled)
