# Fritzing sketch Example-2_ESP32-CAM (saved by Fritzing 0.9.9b)

parts:
  Part1 = Arduino Uno (Rev3) - ICSP
  Mod1 = ESP32-CAM

nets:
  GND: Part1.GND, Part1.RESET, Mod1.GND, Mod1.IO0
  N1: Part1.D0/RX, Mod1.VOR
  N2: Part1.D1/TX, Mod1.VOT
  5V: Part1.5V, Mod1.5V

custom parts:
  ESP32-CAM: The ESP32-CAM has a very competitive small-size camera module that can operate independently as a minimum system with a footprint of only 27*40.5*4.5mm and a deep sleep current of up to 6mA.
