# Fritzing sketch Example-3_IoT-Device (saved by Fritzing 0.9.9b)
breadboards: 1

parts:
  Part1 = Arduino Uno (Rev3) - ICSP
  Mod1 = ESP32-CAM
  R1 = Resistor [tolerance=±1% power=0.25 resistance=220 package=THT]
  LED1 = LED - 3mm [color="Blue (470nm)" current=0.030 package="3 mm [THT]"]

nets:
  GND: Part1.GND, Part1.RESET, Mod1.GND, Mod1.IO0, LED1.cathode
  N1: Part1.D0/RX, Mod1.VOR
  N2: Part1.D1/TX, Mod1.VOT
  5V: Part1.5V, Mod1.5V
  N3: Mod1.IO4, R1.Pin_0
  N4: R1.Pin_1, LED1.anode

custom parts:
  ESP32-CAM: The ESP32-CAM has a very competitive small-size camera module that can operate independently as a minimum system with a footprint of only 27*40.5*4.5mm and a deep sleep current of up to 6mA.
