# Fritzing sketch MAX30102_setup (saved by Fritzing 0.9.9b)

parts:
  Part1 = Arduino Uno (Rev3)
  M1 = MAX30102

nets:
  N1: Part1.A5/SCL, M1.SCL
  N2: Part1.A4/SDA, M1.SDA
  5V: Part1.5V, M1.VIN
  GND: Part1.GND, M1.GND

custom parts:
  MAX30102: Pulse-Oximeter module using the MAX30102 chip. As usual, if you want the mounting holes in pcb, you need to drag a hole over the pad in silkscreen to actually drill the hole (by default they are not drilled)
